# Fritzing sketch Diagrama (saved by Fritzing 0.9.3b)
breadboards: 1

parts:
  U1 = LCD-16X2 [package=lcd-16x2_noholes]
  Componente1 = Arduino Uno (Rev3)
  R1 = Photocell (LDR) [package=THT]
  R2 = Resistor [tolerance=±0.05% resistance=330 package=THT]
  RHT1 = Humidity and Temperature Sensor RHT03
  R4 = Trimmer Potentiometer [maximum_resistance=10kΩ package=THT]
  S1 = Pushbutton [package=THT]
  R5 = Resistor [tolerance=±0.5% resistance=10k package="2512 [SMD]"]

nets:
  N1: U1.VSS, U1.R_W, U1.K, R2.Pin_1, RHT1.GND_1, R4.leg2, R5.Pin_1
  VDD: U1.VDD, U1.A, R1.pin_0, RHT1.Vcc, R4.leg1, S1.leg1
  N2: U1.VO, R4.wiper
  N3: U1.RS, Componente1.D12/MISO
  N4: U1.E, Componente1.D11_PWM/MOSI
  N5: U1.DB4, Componente1.D6_PWM
  N6: U1.DB5, Componente1.D5_PWM
  N7: U1.DB6, Componente1.D4
  N8: U1.DB7, Componente1.D3_PWM
  N9: Componente1.A0, R1.pin_1, R2.Pin_0
  N10: Componente1.D2, RHT1.Data-signal
  N11: S1.leg0, R5.Pin_0
